// Logisim project obJugadorMovsXYcirc.circ as structural Verilog: 3 circuits, main circuit main
module main (
  output [3:0] pos_x,
  output [2:0] pos_y
);

  wire clock_1_out, clock_2_out, clock_3_out, der_out, down_out, et1, et2, et3, et4, et5, et6, et7, et8, et9,
       et10, et11, et12, et13, et14, et15, et16, izq_out, up_out;
  wire [15:0] shift_register_1_p3, shift_register_3_p11;

  Clock clock_1 (.out(clock_1_out));
  Clock clock_2 (.out(clock_2_out));
  Clock clock_3 (.out(clock_3_out));
  // Shift_Register #(.length(16)) shift_register_1: pin names not known; wires that end beside it: clock_1_out, shift_register_1_p3[15], shift_register_1_p3[0], shift_register_1_p3[1], shift_register_1_p3[2], shift_register_1_p3[3], shift_register_1_p3[4], shift_register_1_p3[5], shift_register_1_p3[6], shift_register_1_p3[7]
  // Shift_Register #(.length(16)) shift_register_2: pin names not known; wires that end beside it: clock_2_out, et16, shift_register_1_p3[15], shift_register_1_p3[8], shift_register_1_p3[9], shift_register_1_p3[10], shift_register_1_p3[11], shift_register_1_p3[12], shift_register_1_p3[13], shift_register_1_p3[14], et1, et2, et3, et4, et5, et6, et7, et8
  // Shift_Register #(.length(16)) shift_register_3: pin names not known; wires that end beside it: clock_3_out, shift_register_3_p11[15], et16, et9, et10, et11, et12, et13, et14, et15, shift_register_3_p11[0], shift_register_3_p11[1], shift_register_3_p11[2], shift_register_3_p11[3], shift_register_3_p11[4], shift_register_3_p11[5], shift_register_3_p11[6], shift_register_3_p11[7], shift_register_3_p11[8], shift_register_3_p11[9], shift_register_3_p11[10], shift_register_3_p11[11]
  DotMatrix #(.inputtype("row"), .matrixcols(16), .matrixrows(8)) dotmatrix_1 (
    .row1(shift_register_1_p3),
    .row4({et1, et2, et3, et4, et5, et6, et7, et8, et9, et10, et11, et12, et13, et14, et15, et16}),
    .row6(shift_register_3_p11));  // open: row0, row2, row3, row5, row7
  Button izq (.out(izq_out));
  Button up (.out(up_out));
  Button der (.out(der_out));
  Button down (.out(down_out));
  movX movx_1 (.left(izq_out), .right(der_out), .posExit(pos_x));
  movY movy_1 (.down(down_out), .up(up_out), .posExit(pos_y));
endmodule

module movX (
  input  left,
  input  right,
  output [3:0] posExit
);

  wire clock_1_out, comparator_1_gt, comparator_2_lt;
  wire [1:0] and_2_out;
  wire [3:0] adder_1_out, register_1_q, subtractor_1_out;

  Clock clock_1 (.out(clock_1_out));
  Register #(.width(4)) register_1 (.D(posExit), .clk(clock_1_out), .Q(register_1_q));  // open: en, clr
  Comparator #(.mode("unsigned"), .width(4)) comparator_1 (
    .a(register_1_q), .b(4'b0000), .gt(comparator_1_gt));  // open: eq, lt
  Comparator #(.mode("unsigned"), .width(4)) comparator_2 (
    .a(register_1_q), .b(4'b1111), .lt(comparator_2_lt));  // open: gt, eq
  Adder #(.width(4)) adder_1 (.a(register_1_q), .b(4'b0001), .out(adder_1_out));  // open: cin, cout
  Subtractor #(.width(4)) subtractor_1 (.a(register_1_q), .b(4'b0001), .out(subtractor_1_out));  // open: bin, bout
  and and_1 (and_2_out[1], left, comparator_1_gt);
  and and_2 (and_2_out[0], right, comparator_2_lt);
  Multiplexer #(.select(2), .width(4)) multiplexer_1 (
    .in0(register_1_q), .in1(adder_1_out), .in2(subtractor_1_out), .in3(register_1_q), .out(posExit),
    .sel(and_2_out));

  // Notes on the sheet:
  //   x+1 (der)
  //    (01 der)
  //   x-1 (izq)
  //   codificador
  //   aca decide si puede moverse o no
  //   (10 izq)
endmodule

module movY (
  input  down,
  input  up,
  output [2:0] posExit
);

  wire clock_1_out, comparator_1_gt, comparator_2_lt;
  wire [1:0] and_2_out;
  wire [2:0] adder_1_out, register_1_q, subtractor_1_out;

  Clock clock_1 (.out(clock_1_out));
  Register #(.width(3)) register_1 (.D(posExit), .clk(clock_1_out), .Q(register_1_q));  // open: en, clr
  Comparator #(.mode("unsigned"), .width(3)) comparator_1 (
    .a(register_1_q), .b(3'b000), .gt(comparator_1_gt));  // open: eq, lt
  Comparator #(.mode("unsigned"), .width(3)) comparator_2 (
    .a(register_1_q), .b(3'b111), .lt(comparator_2_lt));  // open: gt, eq
  Adder #(.width(3)) adder_1 (.a(register_1_q), .b(3'b001), .out(adder_1_out));  // open: cin, cout
  Subtractor #(.width(3)) subtractor_1 (.a(register_1_q), .b(3'b001), .out(subtractor_1_out));  // open: bin, bout
  and and_1 (and_2_out[1], down, comparator_1_gt);
  and and_2 (and_2_out[0], up, comparator_2_lt);
  Multiplexer #(.select(2), .width(3)) multiplexer_1 (
    .in0(register_1_q), .in1(adder_1_out), .in2(subtractor_1_out), .in3(register_1_q), .out(posExit),
    .sel(and_2_out));

  // Notes on the sheet:
  //   x+1 (der)
  //    (01 der)
  //   x-1 (izq)
  //   codificador
  //   aca decide si puede moverse o no
  //   (10 izq)
endmodule
